# Fritzing sketch MotorControl_28BYJ48 (saved by Fritzing 0.7.11b)
stripboards: 1
breadboards: 1

parts:
  R1 = Rotary Potentiometer (Small) [maximum_resistance=1kΩ]
  IC1 = ULN2003A [package="DIP16 [THT]"]
  M1 = Stepper Motor - Bipolar
  R2 = Resistor [tolerance=±5% resistance=220 package=THT]
  R3 = Resistor [tolerance=±5% resistance=220 package=THT]
  R4 = Resistor [tolerance=±5% resistance=220 package=THT]
  7_Segment1 = 7 Segment Display
  R5 = Resistor [tolerance=±5% resistance=220 package=THT]
  Arduino1 = Arduino

nets:
  N1: R1.leg1, IC1.0V, 7_Segment1.common_anode, Arduino1.GND
  N2: R1.wiper, Arduino1.A0
  N3: R1.leg2, IC1.COM_-_Common, Arduino1.+5V
  N4: IC1.In_1, Arduino1.D8
  N5: IC1.In_2, Arduino1.D9
  N6: IC1.In_3, Arduino1.D10
  N7: IC1.In_4, Arduino1.D11
  N8: IC1.Out_4, M1.D, R2.Pin_1
  N9: IC1.Out_3, M1.B, R3.Pin_1
  N10: IC1.Out_2, M1.C, R4.Pin_1
  N11: IC1.Out_1, M1.A, R5.Pin_1
  N12: R2.Pin_0, 7_Segment1.Segment_A
  N13: R3.Pin_0, 7_Segment1.Segment_C, 7_Segment1.Segment_B
  N14: R4.Pin_0, 7_Segment1.Segment_D
  N15: 7_Segment1.Segment_F, 7_Segment1.Segment_E, R5.Pin_0

notes:
  real one is ULN2003AN
  Stepper Motor 28BYJ-48
  wire color of component doesn't match with real motor
